# Fritzing sketch SeedOsc (saved by Fritzing 0.9.4)
breadboards: 1

parts:
  SOM1 = Daisy Seed [chip_label=IC package="DIP (Dual Inline) [THT]"]
  R1 = Rotary Potentiometer (Small) [maximum_resistance=100kΩ package=THT]
  S1 = Pushbutton [package="[THT]"]
  SPKR1 = Loudspeaker

nets:
  N1: SOM1.pin_19, SPKR1.pin2
  GND: SOM1.pin_20, SOM1.pin_40, R1.leg1, S1.Pin_3, S1.Pin_4, SPKR1.pin1
  3.3V: SOM1.pin_21, R1.leg2
  N2: SOM1.pin_28, R1.wiper
  N3: SOM1.pin_35, S1.Pin_1, S1.Pin_2

custom parts:
  Daisy Seed: Daisy is an embedded platform for music. It features everything you need for creating high fidelity audio hardware devices. Just plug in a USB cable and start making sound! No soldering required.
